# Fritzing sketch UP_DOWN_1 (saved by Fritzing 0.9.3b)
breadboards: 1

parts:
  Componente1 = Arduino Uno (Rev3)
  R1 = Resistor [tolerance=±5% resistance=220 package=THT]
  R2 = Resistor [tolerance=±5% resistance=220 package=THT]
  R3 = Resistor [tolerance=±5% resistance=220 package=THT]
  LED1 = LED - 5mm [color="Red (633nm)" package="5 mm [THT]"]  # not connected
  LED2 = LED - 5mm [color="Green (560nm)" package="5 mm [THT]"]  # not connected
  LED3 = LED - 5mm [color="Blue (430nm)" package="5 mm [THT]"]  # not connected

nets:
  N1: Componente1.GND, R1.Pin_0, R2.Pin_0, R3.Pin_0
