# Fritzing sketch W4_Line (saved by Fritzing 0.9.3b)
breadboards: 1

parts:
  Componente1 = Arduino Uno (Rev3)
  R2 = Resistor [tolerance=±5% resistance=220 package=THT]
  R3 = Resistor [tolerance=±5% resistance=220 package=THT]  # not connected
  LED3 = LED - 5mm [color="White (4500K)" package="5 mm [THT]"]  # not connected
  LED4 = LED - 5mm [color="White (4500K)" package="5 mm [THT]"]  # not connected
  LED6 = LED - 5mm [color="White (4500K)" package="5 mm [THT]"]  # not connected
  LED7 = LED - 5mm [color="White (4500K)" package="5 mm [THT]"]  # not connected
  R4 = Resistor [tolerance=±5% resistance=220 package=THT]
  R5 = Resistor [tolerance=±5% resistance=220 package=THT]

nets:
  N1: Componente1.GND, R2.Pin_0, R4.Pin_0, R5.Pin_0
