# Fritzing sketch UP_DOWN_1 (saved by Fritzing 0.9.3b)
breadboards: 1

parts:
  Componente1 = Arduino Uno (Rev3)
  R1 = Resistor [tolerance=±5% resistance=220 package=THT]
  R2 = Resistor [tolerance=±5% resistance=220 package=THT]
  R3 = Resistor [tolerance=±5% resistance=220 package=THT]
  LED1 = LED - 5mm [color="Red (633nm)" package="5 mm [THT]"]
  LED2 = LED - 5mm [color="Green (560nm)" package="5 mm [THT]"]
  LED3 = LED - 5mm [color="Blue (430nm)" package="5 mm [THT]"]  # not connected

nets:
  N1: Componente1.D10_PWM/SS, LED2.cathode
  N2: Componente1.D11_PWM/MOSI, LED1.cathode
  N3: Componente1.GND, R1.Pin_0, R2.Pin_0, R3.Pin_0
  N4: R1.Pin_1, LED2.anode
  N5: R2.Pin_1, LED1.anode
